// Logisim project gate_transistor.circ as structural Verilog: 7 circuits, main circuit main
module main (
  input  in_1,
  input  in_2,
  output out_3
);

  wire nor_gate_1_v_out;

  NOR_GATE nor_gate_1 (.A(in_1), .B(in_2), .V_out(nor_gate_1_v_out));
  Full_Adder full_adder_1 ();  // open: A, B, C_in, S, C_out
  NOTGATE notgate_1 (.A(nor_gate_1_v_out), .V_out(out_3));
endmodule

module NOTGATE (
  input  A,
  output V_out
);

  Pull_Resistor #(.pull(1)) pull_resistor_1 (.node(V_out));
  Transistor #(.\type ("n")) transistor_1 (.in(1'b0), .out(V_out), .gate(A));

  // Notes on the sheet:
  //   Arrow sign shows the Collector/ Drain
  //   NOT Gate
endmodule

module NAND_GATE (
  input  A,
  input  B,
  output V_out
);

  wire transistor_2_out;

  Pull_Resistor #(.pull(1)) pull_resistor_1 (.node(V_out));
  Transistor #(.\type ("n")) transistor_1 (.in(transistor_2_out), .out(V_out), .gate(A));
  Transistor #(.\type ("n")) transistor_2 (.in(1'b0), .out(transistor_2_out), .gate(B));

  // Notes on the sheet:
  //   NAND Gate
endmodule

module NOR_GATE (
  input  A,
  input  B,
  output V_out
);

  Transistor #(.\type ("n")) transistor_1 (.in(1'b0), .out(V_out), .gate(A));
  Pull_Resistor #(.pull(1)) pull_resistor_1 (.node(V_out));
  Transistor #(.\type ("n")) transistor_2 (.in(1'b0), .out(V_out), .gate(B));

  // Notes on the sheet:
  //   NOR Gate
endmodule

module OR_GATE (
  input  in_1,
  input  in_2,
  output out_3
);

  wire nor_gate_1_v_out;

  NOR_GATE nor_gate_1 (.A(in_1), .B(in_2), .V_out(nor_gate_1_v_out));
  NOTGATE notgate_1 (.A(nor_gate_1_v_out), .V_out(out_3));

  // Notes on the sheet:
  //   OR Gate
endmodule

module AND_GATE (
  input  in_1,
  input  in_2,
  output out_3
);

  wire nand_gate_1_v_out;

  NAND_GATE nand_gate_1 (.A(in_1), .B(in_2), .V_out(nand_gate_1_v_out));
  NOTGATE notgate_1 (.A(nand_gate_1_v_out), .V_out(out_3));
endmodule

module Full_Adder (
  input  A,
  input  B,
  input  C_in,
  output S,
  output C_out
);

  wire and_1_out, and_2_out, xor_1_out;

  xor xor_1 (xor_1_out, A, B);
  xor xor_2 (S, xor_1_out, C_in);
  and and_1 (and_1_out, A, B);
  and and_2 (and_2_out, xor_1_out, C_in);
  or or_1 (C_out, and_1_out, and_2_out);

  // Notes on the sheet:
  //   S = A^B^C_in
  //   C_out = AB + (A^B).C_in
  //   Full Adder
endmodule
